# Fritzing sketch IMU_LED_sketch (saved by Fritzing 1.0.4)
breadboards: 1

parts:
  WeMos_D1_Mini1 = WeMos D1 Mini
  Part1 = InvenSense MPU6050
  LED1 = RGB LED (com. cathode, rbg) [color="Red (633nm)" current=0.030A package="5 mm [THT]"]

nets:
  3V3: WeMos_D1_Mini1.3V3, Part1.VCC
  N1: WeMos_D1_Mini1.D1, Part1.SCL
  N2: WeMos_D1_Mini1.D2, Part1.SDA
  N3: WeMos_D1_Mini1.D5, LED1.red_anode
  N4: WeMos_D1_Mini1.D6, LED1.green_anode
  N5: WeMos_D1_Mini1.D7, LED1.blue_anode
  N6: WeMos_D1_Mini1.G, Part1.GND, LED1.common_cathode
